// Logisim project smips.circ as structural Verilog: 4 circuits, main circuit Board
module Board (
);

  wire CLK, HALT, MEM_WE, RESET, TTY_WE;
  wire [3:0] MEM_BE;
  wire [6:0] TTY_DATA;
  wire [31:0] MEM_ADDR, MEM_RDATA, MEM_WDATA;

  Clock Reloj (.out(CLK));
  Button u_Reset (.out(RESET));
  CPU cpu_1 (
    .CLK(CLK), .RESET(RESET), .MEM_RDATA(MEM_RDATA), .MEM_ADDR(MEM_ADDR), .MEM_WDATA(MEM_WDATA),
    .MEM_BE(MEM_BE), .MEM_WE(MEM_WE), .TTY_DATA(TTY_DATA), .TTY_WE(TTY_WE), .HALT(HALT));
  TTY #(.cols(48), .rows(12)) tty_1 (.data(TTY_DATA), .clk(CLK), .we(TTY_WE), .clr(RESET));
  Memory memory_1 (.CLK(CLK), .ADDR(MEM_ADDR), .WDATA(MEM_WDATA), .BE(MEM_BE), .WE(MEM_WE), .RDATA(MEM_RDATA));
  LED u_Halt (.in(HALT));

  // Notes on the sheet:
  //   S-MIPS | Board
  //   No modificar: la CPU se implementa dentro del subcircuito CPU.
endmodule

module CPU (
  input  CLK,
  input  RESET,
  input  [31:0] MEM_RDATA,
  output [31:0] MEM_ADDR,
  output [31:0] MEM_WDATA,
  output [3:0] MEM_BE,
  output MEM_WE,
  output [6:0] TTY_DATA,
  output TTY_WE,
  output HALT
);


  // Notes on the sheet:
  //   CPU S-MIPS: implementar aqui
  //   No cambiar nombres, anchos ni sentido de los pines: la placa depende de ellos.
endmodule

module Memory (
  input  CLK,
  input  [31:0] ADDR,
  input  [31:0] WDATA,
  input  [3:0] BE,
  input  WE,
  output [31:0] RDATA
);

  RAM #(.addrWidth(12), .asyncread("true"), .byteenables("byteEnables"), .dataWidth(32), .\type ("nonvolatile")) Main_Memory (
    .addr(ADDR[13:2]), .we(WE), .oe(1'b1), .clk(CLK), .din(WDATA), .dout(RDATA), .be3(BE[3]), .be2(BE[2]),
    .be1(BE[1]), .be0(BE[0]));

  // Other names for the same wires on the sheet: A[11:0] = ADDR[13:2]

  // Notes on the sheet:
  //   Memoria unificada: 4096 palabras de 32 bits (16 KiB), little-endian
  //   Lectura combinacional; escritura en el flanco de subida de CLK con WE=1, solo en los bytes con BE=1.
  //   Se usan los bits 13..2 de ADDR; los demas se ignoran (el espacio se repite cada 16 KiB).
endmodule

module ALU (
  input  [31:0] in_1,
  input  [31:0] in_2,
  input  [3:0] in_3,
  output [31:0] out_4,
  output out_5
);

  wire comparator_1_eq, comparator_1_gt, comparator_1_lt;
  wire [31:0] and_Gate, Div, Igual, Mayor, Menor, Mult, or_Gate, Resta, Resto, Suma, xor_Gate;

  Adder #(.width(32)) adder_1 (.a(in_1), .b(in_2), .out(Suma));  // open: cin, cout
  Subtractor #(.width(32)) subtractor_1 (.a(in_1), .b(in_2), .out(Resta));  // open: bin, bout
  Multiplier #(.mode("twosComplement"), .width(32)) multiplier_1 (.a(in_1), .b(in_2), .out(Mult));  // open: cin, cout
  Divider #(.mode("twosComplement"), .width(32)) divider_1 (.a(in_1), .b(in_2), .out(Div), .rem(Resto));  // open: upper
  Comparator #(.width(32)) comparator_1 (
    .a(in_1), .b(in_2), .gt(comparator_1_gt), .eq(comparator_1_eq), .lt(comparator_1_lt));
  assign and_Gate = in_1 & in_2;  // AND_Gate and_1, 32 bits wide
  assign or_Gate = in_1 | in_2;  // OR_Gate or_1, 32 bits wide
  assign xor_Gate = in_1 ^ in_2;  // XOR_Gate xor_1, 32 bits wide
  assign Mayor = {{31{comparator_1_gt}}, comparator_1_gt};  // Bit_Extender bit_extender_1
  assign Igual = {{31{comparator_1_eq}}, comparator_1_eq};  // Bit_Extender bit_extender_2
  assign Menor = {{31{comparator_1_lt}}, comparator_1_lt};  // Bit_Extender bit_extender_3
  Multiplexer #(.select(4), .width(32)) multiplexer_1 (
    .in0(Suma), .in1(Resta), .in2(Mult), .in3(Div), .in4(Resto), .in5(and_Gate), .in6(or_Gate),
    .in7(xor_Gate), .in8(Mayor), .in9(Igual), .in10(Menor), .out(out_4), .sel(in_3));  // open: in11, in12, in13, in14, in15
  Comparator #(.width(32)) comparator_2 (.a({32{1'b0}}), .b(out_4), .eq(out_5));  // open: gt, lt

  // Other names for the same wires on the sheet: Rd[31:0] = out_4; Rs[31:0] = in_1; Rt[31:0] = in_2;
  //   Selector_ALU[3:0] = in_3; zero = out_5

  // Notes on the sheet:
  //   Inputs
  //   Outputs
  //   ALU
endmodule
